// Logisim project whyjs.circ as structural Verilog: 12 circuits, main circuit main
module main (
  input  [31:0] in_1,
  input  [31:0] in_2,
  input  [31:0] in_3,
  input  [31:0] in_4
);

  wire [31:0] alu_sll_1_sll_hi, alu_sll_1_sll_lo;

  // Probe on alu_sll_1_sll_hi
  ALU__sll alu_sll_1 (
    .B_lo(in_4), .B_hi(in_3), .sll_hi(alu_sll_1_sll_hi), .sll_lo(alu_sll_1_sll_lo), .A_hi(in_1), .A_lo(in_2));
  // Probe on alu_sll_1_sll_lo
endmodule

module ALU (
  input  [11:0] opcode,
  input  [11:0] funct,
  input  [31:0] A_hi,
  input  [31:0] A_lo,
  input  [31:0] B_hi,
  input  [31:0] B_lo,
  output [31:0] Z_hi,
  output [31:0] Z_lo
);

  wire add_c, adder_1_cout, sub_c, subtractor_1_bout;
  wire [4:0] alu_full_ob_selector_1_sel;
  wire [31:0] add_hi, add_lo, sll_hi, sll_lo, sub_hi, sub_lo;

  Adder #(.width(32)) adder_1 (.a(A_lo), .b(B_lo), .out(add_lo), .cout(adder_1_cout));  // open: cin
  Adder #(.width(32)) adder_2 (.a(A_hi), .b(B_hi), .out(add_hi), .cin(adder_1_cout), .cout(add_c));
  Subtractor #(.width(32)) subtractor_1 (.a(A_lo), .b(B_lo), .out(sub_lo), .bout(subtractor_1_bout));  // open: bin
  Subtractor #(.width(32)) subtractor_2 (.a(A_hi), .b(B_hi), .out(sub_hi), .bin(subtractor_1_bout), .bout(sub_c));
  ALU__sll alu_sll_1 (.B_lo(B_lo), .B_hi(B_hi), .sll_hi(sll_hi), .sll_lo(sll_lo), .A_hi(A_hi), .A_lo(A_lo));
  Multiplexer #(.select(5), .width(32), .enable("false")) multiplexer_1 (
    .in0(add_hi), .in1(sub_hi), .in2(sll_hi), .out(Z_hi), .sel(alu_full_ob_selector_1_sel));  // open: in3, in4, in5, in6, in7, in8, in9, in10, in11, in12, in13, in14, in15, in16, in17, in18, in19, in20, in21, in22, in23, in24, in25, in26, in27, in28, in29, in30, in31
  ALU__Full_OB_Selector alu_full_ob_selector_1 (.opcode(opcode), .funct(funct), .sel(alu_full_ob_selector_1_sel));
  Multiplexer #(.select(5), .width(32), .enable("false")) multiplexer_2 (
    .in0(add_lo), .in1(sub_lo), .in2(sll_lo), .out(Z_lo), .sel(alu_full_ob_selector_1_sel));  // open: in3, in4, in5, in6, in7, in8, in9, in10, in11, in12, in13, in14, in15, in16, in17, in18, in19, in20, in21, in22, in23, in24, in25, in26, in27, in28, in29, in30, in31
endmodule

module ALU__Full_OB_Selector (
  input  [11:0] opcode,
  input  [11:0] funct,
  output [4:0] sel
);

  wire [4:0] alu_rlogic_ob_selector_1_sel, alu_rmath_ob_selector_1_sel;

  ALU__RMath_OB_Selector alu_rmath_ob_selector_1 (.opcode(opcode), .funct(funct), .sel(alu_rmath_ob_selector_1_sel));
  ALU__RLogic_OB_Selector alu_rlogic_ob_selector_1 (.opcode(opcode), .funct(funct), .sel(alu_rlogic_ob_selector_1_sel));
  assign sel = alu_rmath_ob_selector_1_sel | alu_rlogic_ob_selector_1_sel;  // OR_Gate or_1, 5 bits wide
endmodule

module ALU__RMath_OB_Selector (
  input  [11:0] opcode,
  input  [11:0] funct,
  output [4:0] sel
);

  wire comparator_1_eq;
  wire [4:0] and_1_out, and_2_out, and_3_out, and_4_out, and_5_out, and_6_out, and_7_out, and_8_out,
       bit_extender_1_out, constant_cmp_12_5_1_z, constant_cmp_12_5_2_z, constant_cmp_12_5_3_z,
       constant_cmp_12_5_4_z, constant_cmp_12_5_5_z, constant_cmp_12_5_6_z, constant_cmp_12_5_7_z,
       constant_cmp_12_5_8_z, or_1_out, or_3_out;

  Comparator #(.width(12)) comparator_1 (.a(opcode), .b(12'h1), .eq(comparator_1_eq));  // open: gt, lt
  assign bit_extender_1_out = {{4{comparator_1_eq}}, comparator_1_eq};  // Bit_Extender bit_extender_1
  Constant_Cmp_12_5 constant_cmp_12_5_1 (.A(funct), .B({12{1'b0}}), .Z(constant_cmp_12_5_1_z), .outconst({5{1'b0}}));
  Constant_Cmp_12_5 constant_cmp_12_5_2 (.A(funct), .B(12'h1), .Z(constant_cmp_12_5_2_z), .outconst(5'b00001));
  Constant_Cmp_12_5 constant_cmp_12_5_3 (.A(funct), .B(12'h2), .Z(constant_cmp_12_5_3_z), .outconst(5'b00010));
  Constant_Cmp_12_5 constant_cmp_12_5_4 (.A(funct), .B(12'h5), .Z(constant_cmp_12_5_4_z), .outconst(5'b00011));
  Constant_Cmp_12_5 constant_cmp_12_5_5 (.A(funct), .B(12'h6), .Z(constant_cmp_12_5_5_z), .outconst(5'b00100));
  Constant_Cmp_12_5 constant_cmp_12_5_6 (.A(funct), .B(12'h7), .Z(constant_cmp_12_5_6_z), .outconst(5'b00101));
  Constant_Cmp_12_5 constant_cmp_12_5_7 (.A(funct), .B(12'h8), .Z(constant_cmp_12_5_7_z), .outconst(5'b00110));
  Constant_Cmp_12_5 constant_cmp_12_5_8 (.A(funct), .B(12'h9), .Z(constant_cmp_12_5_8_z), .outconst(5'b00111));
  assign and_1_out = constant_cmp_12_5_1_z & bit_extender_1_out;  // AND_Gate and_1, 5 bits wide
  assign and_2_out = constant_cmp_12_5_2_z & bit_extender_1_out;  // AND_Gate and_2, 5 bits wide
  assign and_3_out = constant_cmp_12_5_3_z & bit_extender_1_out;  // AND_Gate and_3, 5 bits wide
  assign and_4_out = constant_cmp_12_5_4_z & bit_extender_1_out;  // AND_Gate and_4, 5 bits wide
  assign and_5_out = constant_cmp_12_5_5_z & bit_extender_1_out;  // AND_Gate and_5, 5 bits wide
  assign and_6_out = constant_cmp_12_5_6_z & bit_extender_1_out;  // AND_Gate and_6, 5 bits wide
  assign and_7_out = constant_cmp_12_5_7_z & bit_extender_1_out;  // AND_Gate and_7, 5 bits wide
  assign and_8_out = constant_cmp_12_5_8_z & bit_extender_1_out;  // AND_Gate and_8, 5 bits wide
  assign or_1_out = and_1_out | and_2_out | and_3_out | and_4_out;  // OR_Gate or_1, 5 bits wide
  assign sel = or_1_out | or_3_out;  // OR_Gate or_2, 5 bits wide
  assign or_3_out = and_5_out | and_6_out | and_7_out | and_8_out;  // OR_Gate or_3, 5 bits wide

  // Notes on the sheet:
  //   Calculates select bit for output mux for R-type math
endmodule

module ALU__RLogic_OB_Selector (
  input  [11:0] opcode,
  input  [11:0] funct,
  output [4:0] sel
);

  wire comparator_1_eq;
  wire [4:0] and_1_out, and_2_out, and_3_out, and_4_out, and_5_out, and_6_out, and_7_out, and_8_out,
       and_9_out, and_10_out, and_11_out, and_12_out, and_13_out, and_14_out, bit_extender_1_out,
       constant_cmp_12_5_1_z, constant_cmp_12_5_2_z, constant_cmp_12_5_3_z, constant_cmp_12_5_4_z,
       constant_cmp_12_5_5_z, constant_cmp_12_5_6_z, constant_cmp_12_5_7_z, constant_cmp_12_5_8_z,
       constant_cmp_12_5_9_z, constant_cmp_12_5_10_z, constant_cmp_12_5_11_z, constant_cmp_12_5_12_z,
       constant_cmp_12_5_13_z, constant_cmp_12_5_14_z, or_1_out, or_2_out;

  Comparator #(.width(12)) comparator_1 (.a(opcode), .b(12'h2), .eq(comparator_1_eq));  // open: gt, lt
  assign bit_extender_1_out = {{4{comparator_1_eq}}, comparator_1_eq};  // Bit_Extender bit_extender_1
  Constant_Cmp_12_5 constant_cmp_12_5_1 (.A(funct), .B({12{1'b0}}), .Z(constant_cmp_12_5_1_z), .outconst(5'b01000));
  Constant_Cmp_12_5 constant_cmp_12_5_2 (.A(funct), .B(12'h1), .Z(constant_cmp_12_5_2_z), .outconst(5'b01001));
  Constant_Cmp_12_5 constant_cmp_12_5_3 (.A(funct), .B(12'h2), .Z(constant_cmp_12_5_3_z), .outconst(5'b01010));
  Constant_Cmp_12_5 constant_cmp_12_5_4 (.A(funct), .B(12'h3), .Z(constant_cmp_12_5_4_z), .outconst(5'b01011));
  Constant_Cmp_12_5 constant_cmp_12_5_5 (.A(funct), .B(12'h4), .Z(constant_cmp_12_5_5_z), .outconst(5'b01100));
  Constant_Cmp_12_5 constant_cmp_12_5_6 (.A(funct), .B(12'h5), .Z(constant_cmp_12_5_6_z), .outconst(5'b01101));
  Constant_Cmp_12_5 constant_cmp_12_5_7 (.A(funct), .B(12'h6), .Z(constant_cmp_12_5_7_z), .outconst(5'b01110));
  Constant_Cmp_12_5 constant_cmp_12_5_8 (.A(funct), .B(12'h8), .Z(constant_cmp_12_5_8_z), .outconst(5'b01111));
  Constant_Cmp_12_5 constant_cmp_12_5_9 (.A(funct), .B(12'h9), .Z(constant_cmp_12_5_9_z), .outconst(5'b10000));
  Constant_Cmp_12_5 constant_cmp_12_5_10 (.A(funct), .B(12'ha), .Z(constant_cmp_12_5_10_z), .outconst(5'b10001));
  Constant_Cmp_12_5 constant_cmp_12_5_11 (.A(funct), .B(12'hb), .Z(constant_cmp_12_5_11_z), .outconst(5'b10010));
  Constant_Cmp_12_5 constant_cmp_12_5_12 (.A(funct), .B(12'hc), .Z(constant_cmp_12_5_12_z), .outconst(5'b10011));
  Constant_Cmp_12_5 constant_cmp_12_5_13 (.A(funct), .B(12'hd), .Z(constant_cmp_12_5_13_z), .outconst(5'b10100));
  Constant_Cmp_12_5 constant_cmp_12_5_14 (.A(funct), .B(12'he), .Z(constant_cmp_12_5_14_z), .outconst(5'b10101));
  assign and_1_out = constant_cmp_12_5_1_z & bit_extender_1_out;  // AND_Gate and_1, 5 bits wide
  assign and_2_out = constant_cmp_12_5_2_z & bit_extender_1_out;  // AND_Gate and_2, 5 bits wide
  assign and_3_out = constant_cmp_12_5_3_z & bit_extender_1_out;  // AND_Gate and_3, 5 bits wide
  assign and_4_out = constant_cmp_12_5_4_z & bit_extender_1_out;  // AND_Gate and_4, 5 bits wide
  assign and_5_out = constant_cmp_12_5_5_z & bit_extender_1_out;  // AND_Gate and_5, 5 bits wide
  assign and_6_out = constant_cmp_12_5_6_z & bit_extender_1_out;  // AND_Gate and_6, 5 bits wide
  assign and_7_out = constant_cmp_12_5_7_z & bit_extender_1_out;  // AND_Gate and_7, 5 bits wide
  assign and_8_out = constant_cmp_12_5_8_z & bit_extender_1_out;  // AND_Gate and_8, 5 bits wide
  assign and_9_out = constant_cmp_12_5_9_z & bit_extender_1_out;  // AND_Gate and_9, 5 bits wide
  assign and_10_out = constant_cmp_12_5_10_z & bit_extender_1_out;  // AND_Gate and_10, 5 bits wide
  assign and_11_out = constant_cmp_12_5_11_z & bit_extender_1_out;  // AND_Gate and_11, 5 bits wide
  assign and_12_out = constant_cmp_12_5_12_z & bit_extender_1_out;  // AND_Gate and_12, 5 bits wide
  assign and_13_out = constant_cmp_12_5_13_z & bit_extender_1_out;  // AND_Gate and_13, 5 bits wide
  assign and_14_out = constant_cmp_12_5_14_z & bit_extender_1_out;  // AND_Gate and_14, 5 bits wide
  assign or_1_out = and_1_out | and_2_out | and_3_out | and_4_out | and_5_out | and_6_out | and_7_out;  // OR_Gate or_1, 5 bits wide
  assign or_2_out = and_8_out | and_9_out | and_10_out | and_11_out | and_12_out | and_13_out | and_14_out;  // OR_Gate or_2, 5 bits wide
  assign sel = or_1_out | or_2_out;  // OR_Gate or_3, 5 bits wide

  // Notes on the sheet:
  //   and
  //   nand
  //   nor
  //   not
  //   or
  //   xnor
  //   xor
  //   land
  //   lnand
  //   lnor
  //   lnot
  //   lor
  //   lxor
  //   lxnor
  //   Calculates select bit for output mux for R-type logic
endmodule

module ALU__mult (
  input  [31:0] A_hi,
  input  [31:0] A_lo,
  input  [31:0] B_hi,
  input  [31:0] B_lo
);
endmodule

module ALU__sll (
  input  [31:0] A_lo,
  input  [31:0] A_hi,
  input  [31:0] B_lo,
  input  [31:0] B_hi,
  output [31:0] sll_hi,
  output [31:0] sll_lo
);

  wire and_1_out, comparator_1_eq, comparator_2_eq;
  wire [31:0] bit_extender_1_out, n64_bit_shifter_6_shift_bits_1_z_hi, n64_bit_shifter_6_shift_bits_1_z_lo;

  _64_bit_Shifter__6_shift_bits u_64_bit_shifter_6_shift_bits_1 (
    .S(B_lo[5:0]), .X_hi(A_hi), .X_lo(A_lo), .Z_hi(n64_bit_shifter_6_shift_bits_1_z_hi),
    .Z_lo(n64_bit_shifter_6_shift_bits_1_z_lo));
  assign bit_extender_1_out = {{6{1'b0}}, B_lo[31:6]};  // Bit_Extender bit_extender_1
  Comparator #(.width(32)) comparator_1 (.a(bit_extender_1_out), .b({32{1'b0}}), .eq(comparator_1_eq));  // open: gt, lt
  Comparator #(.width(32)) comparator_2 (.a({32{1'b0}}), .b(B_hi), .eq(comparator_2_eq));  // open: gt, lt
  Multiplexer #(.width(32), .enable("false")) multiplexer_1 (
    .in0({32{1'b0}}), .in1(n64_bit_shifter_6_shift_bits_1_z_lo), .out(sll_lo), .sel(and_1_out));
  Multiplexer #(.width(32), .enable("false")) multiplexer_2 (
    .in0({32{1'b0}}), .in1(n64_bit_shifter_6_shift_bits_1_z_hi), .out(sll_hi), .sel(and_1_out));
  and and_1 (and_1_out, comparator_1_eq, comparator_2_eq);
endmodule

module Double_Cmp_12_1 (
  input  [11:0] X,
  input  [11:0] A,
  input  [11:0] B,
  input  [11:0] Y,
  output Z
);

  wire comparator_1_eq, comparator_2_eq;

  Comparator #(.width(12)) comparator_1 (.a(X), .b(A), .eq(comparator_1_eq));  // open: gt, lt
  and and_1 (Z, comparator_1_eq, comparator_2_eq);
  Comparator #(.width(12)) comparator_2 (.a(B), .b(Y), .eq(comparator_2_eq));  // open: gt, lt
endmodule

module Double_Cmp_12_32 (
  input  [11:0] X,
  input  [11:0] A,
  input  [11:0] B,
  input  [11:0] Y,
  output [31:0] Z
);

  wire and_1_out, comparator_1_eq, comparator_2_eq;

  Comparator #(.width(12)) comparator_1 (.a(X), .b(A), .eq(comparator_1_eq));  // open: gt, lt
  and and_1 (and_1_out, comparator_1_eq, comparator_2_eq);
  Comparator #(.width(12)) comparator_2 (.a(B), .b(Y), .eq(comparator_2_eq));  // open: gt, lt
  assign Z = {{31{and_1_out}}, and_1_out};  // Bit_Extender bit_extender_1
endmodule

module Constant_Cmp_12_5 (
  input  [4:0] outconst,
  input  [11:0] A,
  input  [11:0] B,
  output [4:0] Z
);

  wire comparator_1_eq;
  wire [4:0] bit_extender_1_out;

  Comparator #(.width(12)) comparator_1 (.a(A), .b(B), .eq(comparator_1_eq));  // open: gt, lt
  assign bit_extender_1_out = {{4{comparator_1_eq}}, comparator_1_eq};  // Bit_Extender bit_extender_1
  assign Z = outconst & bit_extender_1_out;  // AND_Gate and_1, 5 bits wide
endmodule

module _64_bit_Shifter__5_shift_bits (
  input  [31:0] X_lo,
  input  [31:0] X_hi,
  input  [4:0] S,
  output [31:0] Z_lo,
  output [31:0] Z_hi
);

  wire comparator_1_eq;
  wire [4:0] adder_1_out, subtractor_1_out;
  wire [5:0] B_lo;
  wire [31:0] A_hi, A_lo, multiplexer_2_out, or_1_out, shifter_2_out, shifter_3_out, shifter_4_out,
       shifter_5_out, shifter_6_out, shifter_7_out, shifter_8_out, shifter_9_out, shifter_10_out,
       shifter_11_out;

  Shifter #(.width(32)) shifter_1 (.in(X_lo), .\dist (S), .out(Z_lo));
  Comparator #(.width(5)) comparator_1 (.a(S), .b({5{1'b0}}), .eq(comparator_1_eq));  // open: gt, lt
  Shifter #(.width(32)) shifter_2 (.in(X_hi), .\dist (S), .out(shifter_2_out));
  Subtractor #(.width(5)) subtractor_1 (.a({5{1'b1}}), .b(S), .out(subtractor_1_out));  // open: bin, bout
  assign or_1_out = shifter_2_out | shifter_5_out;  // OR_Gate or_1, 32 bits wide
  Shifter #(.width(32), .shift("rl")) shifter_3 (.in(X_lo), .\dist (S), .out(shifter_3_out));
  Shifter #(.width(32)) shifter_4 (.in(shifter_3_out), .\dist (adder_1_out), .out(shifter_4_out));
  Adder #(.width(5)) adder_1 (.a(subtractor_1_out), .b(5'b00001), .out(adder_1_out));  // open: cin, cout
  Multiplexer #(.width(32), .enable("false")) multiplexer_1 (
    .in0(or_1_out), .in1(X_hi), .out(Z_hi), .sel(comparator_1_eq));
  Shifter #(.width(32), .shift("lr")) shifter_5 (.in(shifter_4_out), .\dist (adder_1_out), .out(shifter_5_out));
  Shifter #(.width(32)) shifter_6 (.in(A_lo), .\dist (B_lo[4:0]), .out(shifter_6_out));
  Shifter #(.width(32)) shifter_7 (.in(shifter_6_out), .\dist (5'b10110), .out(shifter_7_out));
  Shifter #(.width(32)) shifter_8 (.in(A_hi), .\dist (B_lo[4:0]), .out(shifter_8_out));
  Shifter #(.width(32)) shifter_9 (.in(shifter_8_out), .\dist (5'b10110), .out(shifter_9_out));
  Shifter #(.width(32)) shifter_10 (.in(shifter_7_out), .\dist (5'b10110), .out(shifter_10_out));
  Shifter #(.width(32)) shifter_11 (.in(shifter_9_out), .\dist (5'b10110), .out(shifter_11_out));
  Multiplexer #(.width(32), .enable("false")) multiplexer_2 (
    .in0(shifter_6_out), .in1(shifter_10_out), .out(multiplexer_2_out), .sel(B_lo[5]));
  Multiplexer #(.width(32), .enable("false")) multiplexer_3 (
    .in0(shifter_8_out), .in1(shifter_11_out), .sel(B_lo[5]));  // open: out
endmodule

module _64_bit_Shifter__6_shift_bits (
  input  [31:0] X_hi,
  input  [31:0] X_lo,
  input  [5:0] S,
  output [31:0] Z_hi,
  output [31:0] Z_lo
);

  wire [5:0] B_lo;
  wire [31:0] A_hi, A_lo, multiplexer_3_out, n64_bit_shifter_5_shift_bits_1_z_hi,
       n64_bit_shifter_5_shift_bits_1_z_lo, n64_bit_shifter_5_shift_bits_2_z_hi,
       n64_bit_shifter_5_shift_bits_2_z_lo, shifter_1_out, shifter_2_out, shifter_3_out, shifter_4_out,
       shifter_5_out, shifter_6_out;

  _64_bit_Shifter__5_shift_bits u_64_bit_shifter_5_shift_bits_1 (
    .X_lo(X_lo), .S(S[4:0]), .Z_lo(n64_bit_shifter_5_shift_bits_1_z_lo),
    .Z_hi(n64_bit_shifter_5_shift_bits_1_z_hi), .X_hi(X_hi));
  _64_bit_Shifter__5_shift_bits u_64_bit_shifter_5_shift_bits_2 (
    .X_lo(n64_bit_shifter_5_shift_bits_1_z_lo), .S(5'b10000), .Z_lo(n64_bit_shifter_5_shift_bits_2_z_lo),
    .Z_hi(n64_bit_shifter_5_shift_bits_2_z_hi), .X_hi(n64_bit_shifter_5_shift_bits_1_z_hi));
  Multiplexer #(.width(32), .enable("false")) multiplexer_1 (
    .in0(n64_bit_shifter_5_shift_bits_1_z_hi), .in1(n64_bit_shifter_5_shift_bits_2_z_hi), .out(Z_hi),
    .sel(S[5]));
  Multiplexer #(.width(32), .enable("false")) multiplexer_2 (
    .in0(n64_bit_shifter_5_shift_bits_1_z_lo), .in1(n64_bit_shifter_5_shift_bits_2_z_lo), .out(Z_lo),
    .sel(S[5]));
  Shifter #(.width(32)) shifter_1 (.in(A_lo), .\dist (B_lo[4:0]), .out(shifter_1_out));
  Shifter #(.width(32)) shifter_2 (.in(shifter_1_out), .\dist (5'b10110), .out(shifter_2_out));
  Shifter #(.width(32)) shifter_3 (.in(A_hi), .\dist (B_lo[4:0]), .out(shifter_3_out));
  Shifter #(.width(32)) shifter_4 (.in(shifter_3_out), .\dist (5'b10110), .out(shifter_4_out));
  Shifter #(.width(32)) shifter_5 (.in(shifter_2_out), .\dist (5'b10110), .out(shifter_5_out));
  Shifter #(.width(32)) shifter_6 (.in(shifter_4_out), .\dist (5'b10110), .out(shifter_6_out));
  Multiplexer #(.width(32), .enable("false")) multiplexer_3 (
    .in0(shifter_1_out), .in1(shifter_5_out), .out(multiplexer_3_out), .sel(B_lo[5]));
  Multiplexer #(.width(32), .enable("false")) multiplexer_4 (
    .in0(shifter_3_out), .in1(shifter_6_out), .sel(B_lo[5]));  // open: out
endmodule
